# Fritzing sketch lightphone-stripboard2 (saved by Fritzing 0.9.2b)
stripboards: 1

parts:
  U1 = MCP6004 - Low Power, rail-to-rail Quad Operational Amplifier [part_number=MCP6004]
  R1_(gnd) = Trimmer Potentiometer [maximum_resistance=1MΩ package=THT]
  R2_(light_sensitivity) = Trimmer Potentiometer [maximum_resistance=1MΩ package=THT]
  Mic_(sleeve) = female pin header, 1 pin [form="♀ (female)"]
  Left_(tip) = female pin header, 1 pin [form="♀ (female)"]
  Gnd_(ring_2) = female pin header, 1 pin [form="♀ (female)"]
  Right_(ring_1) = female pin header, 1 pin [form="♀ (female)"]
  C1 = Ceramic Capacitor [capacitance="100 nF" package="0603 [SMD, multilayer]"]
  C2 = Ceramic Capacitor [capacitance="100 nF" package="0603 [SMD, multilayer]"]
  R4 = Resistor [tolerance=±5% resistance=2.2k package=THT]
  C3 = Ceramic Capacitor [capacitance=1nF package="200 mil [THT, multilayer]"]
  R5 = Resistor [tolerance=±5% resistance=220 package=THT]
  R6 = Resistor [tolerance=±5% resistance=100k package=THT]
  R7 = Resistor [tolerance=±5% resistance=47k package=THT]
  R8 = Resistor [tolerance=±5% resistance=47k package=THT]
  R9 = Resistor [tolerance=±5% resistance=47k package=THT]
  R10 = Resistor [tolerance=±5% resistance=47k package=THT]
  R11 = Resistor [tolerance=±5% resistance=100k package=THT]
  Q2 = LTR-301 [part_number=BPW40 package=ltr-301]
  LED1 = smd LED [color="White (4500K)" package="0805 [SMD]"]
  R13 = Resistor [tolerance=±5% resistance=1k package=THT]
  Q3 = NPN-Transistor [package="TO92 [THT]"]
  R3_(audio_level) = Trimmer Potentiometer [maximum_resistance=1MΩ package=THT]
  VCC1 = 4 x AAA Battery Mount

nets:
  N1: U1.OUTA, R13.Pin_0
  N2: U1.-INA, Left_(tip).pin1
  N3: U1.+INA, Right_(ring_1).pin1
  N4: U1.V+, R1_(gnd).leg2, R2_(light_sensitivity).leg2, Q2.C, VCC1.+
  N5: U1.OUTC, U1.-IND, C3.1, R7.Pin_1, R3_(audio_level).leg2
  N6: U1.-INC, C3.0, R10.Pin_0, R11.Pin_0
  N7: U1.+INC, R8.Pin_0, R9.Pin_0
  N8: U1.V-, R1_(gnd).leg1, R2_(light_sensitivity).leg1, C1.0, R8.Pin_1, LED1.cathode, Q3.E, R3_(audio_level).leg1, VCC1.-
  N9: U1.+IND, R6.Pin_1
  N10: U1.OUTD, R5.Pin_1, R6.Pin_0
  N11: R1_(gnd).wiper, Gnd_(ring_2).pin1, C1.1, R4.Pin_1, R7.Pin_0
  N12: R2_(light_sensitivity).wiper, R9.Pin_1, R11.Pin_1, Q2.E
  N13: Mic_(sleeve).pin1, C2.1, R4.Pin_0
  N14: C2.0, R3_(audio_level).wiper
  N15: R5.Pin_0, Q3.B
  N16: R10.Pin_1, Q3.C
  N17: LED1.anode, R13.Pin_1

notes:
  opamp A: differential L/R audio to light
  opamp C: Sawtooth generator
  opamp D: Schmitt trigger
  1 2 3 4 5 6 7 8 9 0 1 2 3 4 5 6
  1 2 3 4 5 6 7 8 9 0 1 2 3 4 5 6 7 8 9 0
